// Logisim project 04.Or_Gate.circ as structural Verilog: 1 circuit, main circuit main
module main (
  input  in_1,
  input  in_2,
  output out_3
);

  Transistor #(.\type ("n")) transistor_1 (.in(1'b1), .out(out_3), .gate(in_2));
  Transistor #(.\type ("n")) transistor_2 (.in(1'b1), .out(out_3), .gate(in_1));
  Pull_Resistor pull_resistor_1 (.node(out_3));
endmodule
