// Logisim project 10.Simple_Tristate_buffer.circ as structural Verilog: 1 circuit, main circuit main
module main (
  input  in_1,
  input  Data,
  output Output
);

  Transistor #(.\type ("n")) transistor_1 (.in(Data), .out(Output), .gate(in_1));

  // Notes on the sheet:
  //   Enable
  //   This is a very simple tristate buffer logic
endmodule
