// Logisim project 12.1_bit_Memory.circ as structural Verilog: 1 circuit, main circuit main
module main (
  input  in_1,
  output out_2
);

  Transistor #(.\type ("n")) transistor_1 (.in(1'b1), .out(out_2), .gate(in_1));
  Transistor #(.\type ("n")) transistor_2 (.in(1'b1), .out(out_2), .gate(out_2));
  Pull_Resistor pull_resistor_1 (.node(out_2));
endmodule
