// Logisim project 13.R_S.circ as structural Verilog: 1 circuit, main circuit main
module main (
  input  R,
  input  S
);

  wire nor_1_out, nor_2_out;

  nor nor_1 (nor_1_out, R, nor_2_out);
  nor nor_2 (nor_2_out, nor_1_out, S);

  // Notes on the sheet:
  //   Q
  //   Not Q
endmodule
