// Logisim project 14.D_Latch.circ as structural Verilog: 1 circuit, main circuit main
module main (
  input  D
);

  wire nor_1_out, nor_2_out, not_1_out;

  not not_1 (not_1_out, D);
  nor nor_1 (nor_1_out, not_1_out, nor_2_out);
  nor nor_2 (nor_2_out, nor_1_out, D);

  // Notes on the sheet:
  //   Q
  //   Not Q
endmodule
