// Logisim project 14.R-S-Latch.circ as structural Verilog: 1 circuit, main circuit main
module main (
  input  R,
  input  S,
  output Q,
  output out_4
);

  Transistor #(.\type ("n")) transistor_1 (.in(1'b0), .out(Q), .gate(R));
  Transistor #(.\type ("n")) transistor_2 (.in(1'b0), .out(out_4), .gate(S));
  Transistor #(.\type ("n")) transistor_3 (.in(1'b0), .out(Q), .gate(out_4));
  Transistor #(.\type ("n")) transistor_4 (.in(1'b0), .out(out_4), .gate(Q));
  Pull_Resistor #(.pull(1)) pull_resistor_1 (.node(Q));
  Pull_Resistor #(.pull(1)) pull_resistor_2 (.node(out_4));

  // Notes on the sheet:
  //   Not Q
endmodule
