// Logisim project 16.D_Latch_With_Enable.circ as structural Verilog: 1 circuit, main circuit main
module main (
  input  Enable,
  input  D
);

  wire and_1_out, and_2_out, nor_1_out, nor_2_out, not_1_out;

  not not_1 (not_1_out, D);
  and and_1 (and_1_out, not_1_out, Enable);
  and and_2 (and_2_out, Enable, D);
  nor nor_1 (nor_1_out, and_1_out, nor_2_out);
  nor nor_2 (nor_2_out, nor_1_out, and_2_out);

  // Notes on the sheet:
  //   This circuit can be changed with putting a capacitor and resistor
  //   Q
  //   Not Q
endmodule
