// Logisim project 16.Full_Adder.circ as structural Verilog: 1 circuit, main circuit main
module main (
  input  Carry,
  input  B,
  input  A,
  output out_4,
  output out_5
);

  wire and_1_out, and_2_out, xor_1_out;

  xor xor_1 (xor_1_out, B, A);
  and and_1 (and_1_out, B, A);
  and and_2 (and_2_out, xor_1_out, Carry);
  xor xor_2 (out_4, Carry, xor_1_out);
  or or_1 (out_5, and_1_out, and_2_out);

  // Notes on the sheet:
  //   Sum
  //   Carry
endmodule
