// Logisim project Nand_Gate.circ as structural Verilog: 1 circuit, main circuit main
module main (
  input  in_1,
  input  in_2,
  output out_3
);

  wire transistor_1_out, transistor_2_out;

  Transistor #(.\type ("n")) transistor_1 (.in(1'b1), .out(transistor_1_out), .gate(in_1));
  Transistor #(.\type ("n")) transistor_2 (.in(transistor_1_out), .out(transistor_2_out), .gate(in_2));
  Pull_Resistor pull_resistor_1 (.node(transistor_2_out));
  Transistor #(.\type ("n")) transistor_3 (.in(1'b0), .out(out_3), .gate(transistor_2_out));
  Pull_Resistor #(.pull(1)) pull_resistor_2 (.node(out_3));
endmodule
