// Logisim project R_S_Latch_With_Enable.circ as structural Verilog: 1 circuit, main circuit main
module main (
  input  R,
  input  Enable,
  input  S
);

  wire and_1_out, and_2_out, nor_1_out, nor_2_out;

  and and_1 (and_1_out, R, Enable);
  and and_2 (and_2_out, Enable, S);
  nor nor_1 (nor_1_out, and_1_out, nor_2_out);
  nor nor_2 (nor_2_out, nor_1_out, and_2_out);

  // Notes on the sheet:
  //   Q
  //   Not Q
endmodule
