// Logisim project Transistor_Xnor.circ as structural Verilog: 1 circuit, main circuit main
module main (
  input  Input_A,
  input  Input_B,
  output A_Xnor_B
);

  wire pull_resistor_1_node, pull_resistor_2_node, transistor_3_out, transistor_4_out, transistor_5_out,
       transistor_6_out, transistor_7_out;

  Pull_Resistor #(.pull(1)) pull_resistor_1 (.node(pull_resistor_1_node));
  Transistor #(.\type ("n")) transistor_1 (.in(1'b0), .out(pull_resistor_1_node), .gate(Input_A));
  Pull_Resistor #(.pull(1)) pull_resistor_2 (.node(pull_resistor_2_node));
  Transistor #(.\type ("n")) transistor_2 (.in(1'b0), .out(pull_resistor_2_node), .gate(Input_B));
  Transistor #(.\type ("n")) transistor_3 (.in(1'b1), .out(transistor_3_out), .gate(pull_resistor_1_node));
  Transistor #(.\type ("n")) transistor_4 (.in(1'b1), .out(transistor_4_out), .gate(Input_A));
  Transistor #(.\type ("n")) transistor_5 (.in(transistor_3_out), .out(transistor_5_out), .gate(Input_B));
  Transistor #(.\type ("n")) transistor_6 (.in(transistor_4_out), .out(transistor_6_out), .gate(pull_resistor_2_node));
  Pull_Resistor pull_resistor_3 (.node(transistor_5_out));
  Pull_Resistor pull_resistor_4 (.node(transistor_6_out));
  Transistor #(.\type ("n")) transistor_7 (.in(1'b1), .out(transistor_7_out), .gate(transistor_5_out));
  Transistor #(.\type ("n")) transistor_8 (.in(1'b1), .out(transistor_7_out), .gate(transistor_6_out));
  Pull_Resistor pull_resistor_5 (.node(transistor_7_out));
  Pull_Resistor #(.pull(1)) pull_resistor_6 (.node(A_Xnor_B));
  Transistor #(.\type ("n")) transistor_9 (.in(1'b0), .out(A_Xnor_B), .gate(transistor_7_out));

  // Notes on the sheet:
  //   Not A
  //   Not B
  //   Not A And B
  //   A And Not B
  //   A Xor B
endmodule
