// Logisim project Transistor_Xor.circ as structural Verilog: 1 circuit, main circuit main
module main (
  input  Input_A,
  input  Input_B,
  output A_Xor_B
);

  wire transistor_1_out, transistor_2_out, transistor_3_out, transistor_4_out, transistor_5_out,
       transistor_6_out;

  Transistor #(.\type ("n")) transistor_1 (.in(1'b0), .out(transistor_1_out), .gate(Input_A));
  Transistor #(.\type ("n")) transistor_2 (.in(1'b0), .out(transistor_2_out), .gate(Input_B));
  Pull_Resistor #(.pull(1)) pull_resistor_1 (.node(transistor_1_out));
  Pull_Resistor #(.pull(1)) pull_resistor_2 (.node(transistor_2_out));
  Transistor #(.\type ("n")) transistor_3 (.in(1'b1), .out(transistor_3_out), .gate(transistor_1_out));
  Transistor #(.\type ("n")) transistor_4 (.in(1'b1), .out(transistor_4_out), .gate(Input_A));
  Transistor #(.\type ("n")) transistor_5 (.in(transistor_3_out), .out(transistor_5_out), .gate(Input_B));
  Transistor #(.\type ("n")) transistor_6 (.in(transistor_4_out), .out(transistor_6_out), .gate(transistor_2_out));
  Pull_Resistor pull_resistor_3 (.node(transistor_5_out));
  Pull_Resistor pull_resistor_4 (.node(transistor_6_out));
  Transistor #(.\type ("n")) transistor_7 (.in(1'b1), .out(A_Xor_B), .gate(transistor_5_out));
  Transistor #(.\type ("n")) transistor_8 (.in(1'b1), .out(A_Xor_B), .gate(transistor_6_out));
  Pull_Resistor pull_resistor_5 (.node(A_Xor_B));

  // Notes on the sheet:
  //   Not A
  //   Not B
  //   Not A And B
  //   A And Not B
endmodule
