// Logisim project Xnor_Gate.circ as structural Verilog: 1 circuit, main circuit main
module main (
  input  in_1,
  input  in_2,
  output out_3
);

  wire main_1_p2, main_2_p2, main_3_p3, main_4_p3, main_5_p3;

  // Not_Gate_main main_1: pin names not known; wires that end beside it: in_1, main_1_p2
  // Not_Gate_main main_2: pin names not known; wires that end beside it: in_2, main_2_p2
  // And_Gate_main main_3: pin names not known; wires that end beside it: main_2_p2, in_1, main_3_p3
  // And_Gate_main main_4: pin names not known; wires that end beside it: in_2, main_1_p2, main_4_p3
  // Or_Gate_main main_5: pin names not known; wires that end beside it: main_4_p3, main_3_p3, main_5_p3
  // Not_Gate_main main_6: pin names not known; wires that end beside it: main_5_p3, out_3
endmodule
